// Logisim project DEC_Implementation.circ as structural Verilog: 1 circuit, main circuit main
module main (
  input  [6:0] SS
);

  wire and_5_out, and_6_out, and_7_out, and_8_out, and_9_out, and_10_out, and_11_out, and_12_out, and_13_out,
       and_14_out, Clock_out, comparator_1_eq, comparator_1_gt, comparator_2_eq, comparator_2_gt,
       comparator_2_lt, comparator_3_eq, comparator_3_gt, comparator_3_lt, comparator_4_eq, comparator_4_gt,
       comparator_4_lt, comparator_5_eq, comparator_5_lt, decoder_1_out1, decoder_1_out2, decoder_1_out3,
       decoder_1_out4, decoder_1_out5, decoder_2_out1, decoder_2_out2, decoder_2_out3, decoder_2_out4,
       decoder_2_out5, or_1_out, or_2_out, or_3_out, or_4_out, or_6_out, or_7_out, or_8_out, or_9_out,
       or_10_out, or_11_out, or_13_out, or_14_out, or_15_out, or_19_out, or_29_out, or_30_out, or_33_out,
       or_34_out, or_35_out, or_36_out;
  wire [0:0] counter_5_q;
  wire [1:0] counter_3_q, counter_4_q;
  wire [2:0] and_15_out, and_16_out, and_17_out, and_18_out, and_19_out, counter_1_q, counter_2_q,
       counter_6_q, or_5_out;
  wire [2:2] and_1_out, and_2_out, and_3_out, and_4_out, comparator_1_lt;
  wire [4:0] or_16_out, or_21_out, or_26_out, or_31_out;
  wire [4:4] or_32_out;

  Comparator #(.width(7), .mode("unsigned")) comparator_1 (
    .a(7'b1010000), .b(SS), .gt(comparator_1_gt), .eq(comparator_1_eq), .lt(comparator_1_lt[2]));
  Comparator #(.width(7), .mode("unsigned")) comparator_2 (
    .a(7'b0111100), .b(SS), .gt(comparator_2_gt), .eq(comparator_2_eq), .lt(comparator_2_lt));
  Comparator #(.width(7), .mode("unsigned")) comparator_3 (
    .a(7'b0101000), .b(SS), .gt(comparator_3_gt), .eq(comparator_3_eq), .lt(comparator_3_lt));
  Comparator #(.width(7), .mode("unsigned")) comparator_4 (
    .a(7'b0010100), .b(SS), .gt(comparator_4_gt), .eq(comparator_4_eq), .lt(comparator_4_lt));
  Comparator #(.width(7), .mode("unsigned")) comparator_5 (
    .a({7{1'b0}}), .b(SS), .eq(comparator_5_eq), .lt(comparator_5_lt));  // open: gt
  or or_1 (or_1_out, comparator_1_gt, comparator_1_eq);
  and and_1 (and_1_out[2], or_1_out, comparator_2_lt);
  or or_2 (or_2_out, comparator_2_gt, comparator_2_eq);
  and and_2 (and_2_out[2], or_2_out, comparator_3_lt);
  or or_3 (or_3_out, comparator_3_gt, comparator_3_eq);
  and and_3 (and_3_out[2], or_3_out, comparator_4_lt);
  or or_4 (or_4_out, comparator_4_gt, comparator_4_eq);
  and and_4 (and_4_out[2], or_4_out, comparator_5_lt);
  Clock Clock (.out(Clock_out));
  Counter #(.width(3), .max('h7)) counter_1 (
    .Q(counter_1_q), .clk(and_5_out), .clr(and_11_out));  // open: load, D, count, carry
  and and_5 (and_5_out, comparator_1_lt[2], Clock_out);
  Counter #(.width(3), .max('h7)) counter_2 (
    .Q(counter_2_q), .clk(and_6_out), .clr(and_12_out));  // open: load, D, count, carry
  and and_6 (and_6_out, and_1_out[2], Clock_out);
  Counter #(.width(2), .max('h3)) counter_3 (.Q(counter_3_q), .clk(and_7_out));  // open: load, D, count, carry, clr
  and and_7 (and_7_out, and_2_out[2], Clock_out);
  Counter #(.width(2), .max('h3)) counter_4 (
    .Q(counter_4_q), .clk(and_8_out), .clr(and_13_out));  // open: load, D, count, carry
  and and_8 (and_8_out, and_3_out[2], Clock_out);
  Counter #(.width(1), .max('h1)) counter_5 (.Q(counter_5_q[0]), .clk(and_9_out));  // open: load, D, count, carry, clr
  and and_9 (and_9_out, and_4_out[2], Clock_out);
  Counter #(.width(3), .max('h7)) counter_6 (
    .Q(counter_6_q), .clk(and_10_out), .clr(and_14_out));  // open: load, D, count, carry
  and and_10 (and_10_out, comparator_5_eq, Clock_out);
  and and_11 (and_11_out, counter_1_q[2], counter_1_q[1]);
  and and_12 (and_12_out, counter_2_q[2], counter_2_q[0]);
  and and_13 (and_13_out, counter_4_q[1], counter_4_q[0]);
  and and_14 (and_14_out, counter_6_q[2], counter_6_q[1]);
  assign and_15_out = counter_1_q & {3{comparator_1_lt[2]}};  // AND_Gate and_15, 3 bits wide
  assign and_16_out = counter_2_q & {3{and_1_out[2]}};  // AND_Gate and_16, 3 bits wide
  assign and_17_out = {1'b0, counter_3_q} & {3{and_2_out[2]}};  // AND_Gate and_17, 3 bits wide
  assign and_18_out = {1'b0, counter_4_q} & {3{and_3_out[2]}};  // AND_Gate and_18, 3 bits wide
  assign and_19_out = {2'b00, counter_5_q[0]} & {3{and_4_out[2]}};  // AND_Gate and_19, 3 bits wide
  Decoder #(.select(3), .disabled(0)) decoder_1 (
    .out1(decoder_1_out1), .out2(decoder_1_out2), .out3(decoder_1_out3), .out4(decoder_1_out4),
    .out5(decoder_1_out5), .sel(counter_6_q), .en(comparator_5_eq));  // open: out0, out6, out7
  assign or_5_out = and_15_out | and_16_out | and_17_out | and_18_out | and_19_out;  // OR_Gate or_5, 3 bits wide
  Decoder #(.select(3), .disabled(0), .enable("false")) decoder_2 (
    .out1(decoder_2_out1), .out2(decoder_2_out2), .out3(decoder_2_out3), .out4(decoder_2_out4),
    .out5(decoder_2_out5), .sel(or_5_out));  // open: out0, out6, out7
  or or_6 (or_6_out, decoder_1_out1, decoder_1_out5);
  or or_7 (or_7_out, decoder_1_out2, decoder_1_out4);
  or or_8 (or_8_out, decoder_2_out1, decoder_2_out2, decoder_2_out3, decoder_2_out4, decoder_2_out5);
  or or_9 (or_9_out, decoder_2_out2, decoder_2_out3, decoder_2_out4, decoder_2_out5);
  or or_10 (or_10_out, decoder_2_out3, decoder_2_out4, decoder_2_out5);
  or or_11 (or_11_out, decoder_2_out4, decoder_2_out5);
  LED led_1 (.in(or_16_out[4]));
  buf or_12 (or_16_out[4], decoder_1_out3);  // OR_Gate
  LED led_2 (.in(or_13_out));
  buf or_13 (or_13_out, decoder_1_out3);  // OR_Gate
  LED led_3 (.in(or_14_out));
  buf or_14 (or_14_out, decoder_1_out3);  // OR_Gate
  LED led_4 (.in(or_15_out));
  buf or_15 (or_15_out, decoder_1_out3);  // OR_Gate
  or or_16 (or_16_out[0], or_8_out, decoder_1_out3);
  LED led_5 (.in(or_16_out[0]));
  LED led_6 (.in(or_21_out[4]));
  buf or_17 (or_21_out[4], decoder_1_out3);  // OR_Gate
  LED led_7 (.in(or_21_out[3]));
  buf or_18 (or_21_out[3], or_7_out);  // OR_Gate
  LED led_8 (.in(or_19_out));
  buf or_19 (or_19_out, or_7_out);  // OR_Gate
  or or_20 (or_21_out[1], or_9_out, or_7_out);
  LED led_9 (.in(or_21_out[1]));
  or or_21 (or_21_out[0], or_9_out, decoder_1_out3);
  LED led_10 (.in(or_21_out[0]));
  LED led_11 (.in(or_26_out[4]));
  buf or_22 (or_26_out[4], decoder_1_out3);  // OR_Gate
  LED led_12 (.in(or_26_out[3]));
  buf or_23 (or_26_out[3], or_7_out);  // OR_Gate
  LED led_13 (.in(or_26_out[2]));
  or or_24 (or_26_out[2], or_10_out, or_6_out);
  or or_25 (or_26_out[1], or_10_out, or_7_out);
  LED led_14 (.in(or_26_out[1]));
  or or_26 (or_26_out[0], or_10_out, decoder_1_out3);
  LED led_15 (.in(or_26_out[0]));
  DotMatrix #(.matrixrows(5)) dotmatrix_1 (
    .col0({{4{or_16_out[4]}}, or_16_out[0]}), .col1({or_21_out[4:3], or_21_out[3], or_21_out[1:0]}),
    .col2(or_26_out), .col3({or_31_out[4:3], {2{or_31_out[3]}}, or_31_out[0]}), .col4({5{or_32_out[4]}}));
  buf or_27 (or_31_out[4], decoder_1_out3);  // OR_Gate
  LED led_16 (.in(or_31_out[4]));
  or or_28 (or_31_out[3], or_11_out, or_7_out);
  LED led_17 (.in(or_31_out[3]));
  LED led_18 (.in(or_29_out));
  or or_29 (or_29_out, or_11_out, or_7_out);
  or or_30 (or_30_out, or_11_out, or_7_out);
  LED led_19 (.in(or_30_out));
  LED led_20 (.in(or_31_out[0]));
  or or_31 (or_31_out[0], or_11_out, decoder_1_out3);
  or or_32 (or_32_out[4], decoder_2_out5, decoder_1_out3);
  LED led_21 (.in(or_32_out[4]));
  LED led_22 (.in(or_33_out));
  or or_33 (or_33_out, decoder_2_out5, decoder_1_out3);
  or or_34 (or_34_out, decoder_2_out5, decoder_1_out3);
  LED led_23 (.in(or_34_out));
  or or_35 (or_35_out, decoder_2_out5, decoder_1_out3);
  LED led_24 (.in(or_35_out));
  LED led_25 (.in(or_36_out));
  or or_36 (or_36_out, decoder_2_out5, decoder_1_out3);
endmodule
