// Logisim project MUX_Implementation.circ as structural Verilog: 1 circuit, main circuit main
module main (
  input  [6:0] SS_Input
);

  wire and_1_out, and_2_out, and_3_out, and_4_out, and_5_out, clock_1_out, comparator_1_eq, comparator_1_lt,
       comparator_2_eq, comparator_2_gt, comparator_2_lt, comparator_3_eq, comparator_3_gt, comparator_3_lt,
       comparator_4_eq, comparator_4_gt, comparator_4_lt, comparator_5_eq, comparator_5_gt, comparator_5_lt,
       comparator_6_eq, comparator_6_gt, or_1_out, or_2_out, or_3_out, or_4_out, or_5_out;
  wire [3:0] multiplexer_1_out, multiplexer_2_out, multiplexer_3_out, multiplexer_4_out, multiplexer_5_out,
       multiplexer_6_out, multiplexer_7_out, priority_encoder_1_out, register_1_q;
  wire [24:0] multiplexer_8_out;

  Multiplexer #(.select(4), .width(4)) multiplexer_1 (
    .in0(4'b0110), .in1(4'b0000), .in2(4'b0000), .in3(4'b0000), .in4(4'b0000), .in6(4'b0111), .in7(4'b1000),
    .in8(4'b1001), .in9(4'b1010), .in10(4'b0000), .out(multiplexer_1_out), .sel(register_1_q));  // open: in5, in11, in12, in13, in14, in15, en
  Multiplexer #(.select(4), .width(4)) multiplexer_2 (
    .in0(4'b0001), .in1(4'b0000), .in2(4'b0000), .in3(4'b0000), .in4(4'b0000), .in5(4'b0000), .in6(4'b0001),
    .in7(4'b0001), .in8(4'b0001), .in9(4'b0001), .in10(4'b0001), .in11(4'b0001), .in12(4'b0001),
    .in13(4'b0001), .in14(4'b0001), .in15(4'b0001), .out(multiplexer_2_out), .sel(register_1_q));  // open: en
  Multiplexer #(.select(4), .width(4)) multiplexer_3 (
    .in0(4'b0001), .in1(4'b0010), .in2(4'b0000), .in3(4'b0000), .in4(4'b0000), .in5(4'b0010), .in6(4'b0010),
    .in7(4'b0010), .in8(4'b0010), .in9(4'b0010), .in10(4'b0010), .in11(4'b0010), .in12(4'b0010),
    .in13(4'b0010), .in14(4'b0010), .in15(4'b0010), .out(multiplexer_3_out), .sel(register_1_q));  // open: en
  Multiplexer #(.select(4), .width(4)) multiplexer_4 (
    .in0(4'b0001), .in1(4'b0010), .in2(4'b0011), .in3(4'b0000), .in4(4'b0000), .in5(4'b0000), .in6(4'b0000),
    .in7(4'b0011), .in8(4'b0011), .in9(4'b0011), .in10(4'b0011), .in11(4'b0011), .in12(4'b0011),
    .in13(4'b0011), .in14(4'b0011), .in15(4'b0011), .out(multiplexer_4_out), .sel(register_1_q));  // open: en
  Multiplexer #(.select(4), .width(4)) multiplexer_5 (
    .in0(4'b0001), .in1(4'b0010), .in2(4'b0011), .in3(4'b0100), .in4(4'b0000), .in5(4'b0000), .in6(4'b0100),
    .in7(4'b0100), .in8(4'b0100), .in9(4'b0100), .in10(4'b0100), .in11(4'b0100), .in12(4'b0100),
    .in13(4'b0100), .in14(4'b0100), .in15(4'b0100), .out(multiplexer_5_out), .sel(register_1_q));  // open: en
  Multiplexer #(.select(4), .width(4)) multiplexer_6 (
    .in0(4'b0001), .in1(4'b0010), .in2(4'b0011), .in3(4'b0100), .in4(4'b0101), .in5(4'b0000), .in6(4'b0101),
    .in7(4'b0101), .in8(4'b0101), .in9(4'b0101), .in10(4'b0101), .in11(4'b0101), .in12(4'b0101),
    .in13(4'b0101), .in14(4'b0101), .in15(4'b0101), .out(multiplexer_6_out), .sel(register_1_q));  // open: en
  Multiplexer #(.select(4), .width(4)) multiplexer_7 (
    .in0(multiplexer_1_out), .in1(multiplexer_2_out), .in2(multiplexer_3_out), .in3(multiplexer_4_out),
    .in4(multiplexer_5_out), .in5(multiplexer_6_out), .out(multiplexer_7_out), .sel(priority_encoder_1_out));  // open: in6, in7, in8, in9, in10, in11, in12, in13, in14, in15, en
  Clock clock_1 (.out(clock_1_out));
  Register #(.width(4)) register_1 (.D(multiplexer_7_out), .Q(register_1_q), .clk(clock_1_out));  // open: en, clr
  Comparator #(.width(7), .mode("unsigned")) comparator_1 (
    .a(SS_Input), .b(7'b1100100), .eq(comparator_1_eq), .lt(comparator_1_lt));  // open: gt
  Comparator #(.width(7), .mode("unsigned")) comparator_2 (
    .a(SS_Input), .b(7'b1010000), .gt(comparator_2_gt), .eq(comparator_2_eq), .lt(comparator_2_lt));
  Comparator #(.width(7), .mode("unsigned")) comparator_3 (
    .a(SS_Input), .b(7'b0111100), .gt(comparator_3_gt), .eq(comparator_3_eq), .lt(comparator_3_lt));
  Comparator #(.width(7), .mode("unsigned")) comparator_4 (
    .a(SS_Input), .b(7'b0101000), .gt(comparator_4_gt), .eq(comparator_4_eq), .lt(comparator_4_lt));
  Comparator #(.width(7), .mode("unsigned")) comparator_5 (
    .a(SS_Input), .b(7'b0010100), .gt(comparator_5_gt), .eq(comparator_5_eq), .lt(comparator_5_lt));
  Comparator #(.width(7), .mode("unsigned")) comparator_6 (
    .a(SS_Input), .b({7{1'b0}}), .gt(comparator_6_gt), .eq(comparator_6_eq));  // open: lt
  Multiplexer #(.select(4), .width(25)) multiplexer_8 (
    .in0({25{1'b0}}), .in1(25'h1), .in2(25'h61), .in3(25'h1c61), .in4(25'h79c61), .in5(25'h1f79c61),
    .in6(25'h1000), .in7(25'h729c0), .in8(25'h1f8c63f), .in9(25'h729c0), .in10(25'h1000),
    .out(multiplexer_8_out), .sel(register_1_q));  // open: in11, in12, in13, in14, in15, en
  or or_1 (or_1_out, comparator_1_eq, comparator_1_lt);
  or or_2 (or_2_out, comparator_2_gt, comparator_2_eq);
  or or_3 (or_3_out, comparator_3_gt, comparator_3_eq);
  or or_4 (or_4_out, comparator_4_gt, comparator_4_eq);
  or or_5 (or_5_out, comparator_5_gt, comparator_5_eq);
  DotMatrix #(.matrixrows(5)) dotmatrix_1 (
    .col0(multiplexer_8_out[4:0]), .col1(multiplexer_8_out[9:5]), .col2(multiplexer_8_out[14:10]),
    .col3(multiplexer_8_out[19:15]), .col4(multiplexer_8_out[24:20]));
  and and_1 (and_1_out, or_1_out, or_2_out);
  and and_2 (and_2_out, comparator_2_lt, or_3_out);
  and and_3 (and_3_out, comparator_3_lt, or_4_out);
  and and_4 (and_4_out, comparator_4_lt, or_5_out);
  and and_5 (and_5_out, comparator_5_lt, comparator_6_gt);
  Priority_Encoder #(.select(4), .disabled(0)) priority_encoder_1 (
    .in0(comparator_6_eq), .in1(and_5_out), .in2(and_4_out), .in3(and_3_out), .in4(and_2_out),
    .in5(and_1_out), .out(priority_encoder_1_out));  // open: in6, in7, in8, in9, in10, in11, in12, in13, in14, in15, gs, en_out, en_in

  // Notes on the sheet:
  //   SS = 0 (0000)
  //   1 <= SS <= 20 (0001)
  //   21 <= SS <= 40 (0010)
  //   41 <= SS <= 60 (0011)
  //   61 <= SS <= 80 (0100)
  //   81 <= SS <= 100 (0101)
  //   Clock
  //   CENTER 1
  //   LARGE CIRCLE
  //   CENTER 2
  //   BLANK
  //   1 BAR
  //   2 BARS
  //   3 BARS
  //   4 BARS
  //   5 BARS
  //   TINY 1
  //   TINY 2
endmodule
